# Fritzing sketch more_than_one_analog_inputs (saved by Fritzing 0.8.3b)
breadboards: 1

parts:
  Part1 = Arduino Uno (Rev3)
  R1 = Rotary Potentiometer (Small)
  R2 = Rotary Potentiometer (Small)
  R3 = Rotary Potentiometer (Small)
  R4 = Rotary Potentiometer (Small)
  R5 = Rotary Potentiometer (Small)
  R6 = Rotary Potentiometer (Small)

nets:
  N1: Part1.A0, R1.wiper
  N2: Part1.A1, R2.wiper
  N3: Part1.A2, R3.wiper
  N4: Part1.A3, R4.wiper
  N5: Part1.A4/SDA, R5.wiper
  N6: Part1.A5/SCL, R6.wiper
  N7: Part1.GND, R1.leg2, R2.leg2, R3.leg2, R4.leg2, R5.leg2, R6.leg2
  N8: Part1.5V, R1.leg1, R2.leg1, R3.leg1, R4.leg1, R5.leg1, R6.leg1
