# Fritzing sketch servo_motors2 (saved by Fritzing 0.8.3b)
breadboards: 1

parts:
  Part1 = Arduino Uno (Rev3)
  J1 = Basic Servo
  J2 = Basic Servo

nets:
  GND: Part1.GND, J1.gnd, J2.gnd
  N1: Part1.D9_PWM, J2.pulse
  N2: Part1.D3_PWM, J1.pulse
  VCC: Part1.5V, J1.vcc, J2.vcc
